// Logisim project 8bitcomputer.circ as structural Verilog
module _4_bit__carry_fast (
  input  A0,
  input  A1,
  input  A2,
  input  A3,
  input  B0,
  input  B1,
  input  B2,
  input  B3,
  input  Cin,
  output S0,
  output S1,
  output S2,
  output S3,
  output Cout
);

  wire and_1_out, and_2_out, and_3_out, and_4_out, and_5_out, and_6_out, and_7_out, and_8_out, and_9_out,
       and_10_out, and_11_out, and_12_out, and_13_out, and_14_out, and_15_out, and_16_out, and_17_out,
       and_18_out, and_19_out, or_1_out, or_2_out, or_3_out, or_4_out, or_5_out, or_6_out, or_7_out,
       or_8_out, xor_2_out, xor_3_out, xor_4_out, xor_6_out, xor_7_out, xor_8_out, xor_10_out, xor_11_out,
       xor_12_out, xor_13_out, xor_15_out, xor_16_out, xor_17_out, xor_18_out;

  xor xor_1 (S0, Cin, xor_3_out);
  xor xor_2 (xor_2_out, A1, B1);
  xor xor_3 (xor_3_out, A0, B0);
  xor xor_4 (xor_4_out, A0, B0);
  and and_1 (and_1_out, xor_4_out, Cin);
  and and_2 (and_2_out, A0, B0);
  or or_1 (or_1_out, and_1_out, and_2_out);
  xor xor_5 (S1, xor_2_out, or_1_out);
  xor xor_6 (xor_6_out, A2, B2);
  xor xor_7 (xor_7_out, A1, B1);
  xor xor_8 (xor_8_out, A0, B0);
  and and_3 (and_3_out, xor_8_out, Cin);
  or or_2 (or_2_out, and_3_out, and_5_out);
  and and_4 (and_4_out, xor_7_out, or_2_out);
  xor xor_9 (S2, xor_6_out, or_3_out);
  and and_5 (and_5_out, A0, B0);
  and and_6 (and_6_out, A1, B1);
  or or_3 (or_3_out, and_4_out, and_6_out);
  xor xor_10 (xor_10_out, A2, B2);
  xor xor_11 (xor_11_out, A3, B3);
  xor xor_12 (xor_12_out, A1, B1);
  and and_7 (and_7_out, xor_10_out, and_10_out);
  xor xor_13 (xor_13_out, A0, B0);
  and and_8 (and_8_out, A0, B0);
  and and_9 (and_9_out, xor_13_out, Cin);
  or or_4 (or_4_out, and_9_out, and_8_out);
  and and_10 (and_10_out, xor_12_out, or_4_out);
  or or_5 (or_5_out, and_7_out, and_11_out);
  xor xor_14 (S3, xor_11_out, or_5_out);
  xor xor_15 (xor_15_out, A3, B3);
  and and_11 (and_11_out, A2, B2);
  xor xor_16 (xor_16_out, A0, B0);
  xor xor_17 (xor_17_out, A1, B1);
  xor xor_18 (xor_18_out, A2, B2);
  and and_12 (and_12_out, xor_16_out, Cin);
  and and_13 (and_13_out, xor_17_out, or_6_out);
  and and_14 (and_14_out, xor_18_out, or_7_out);
  and and_15 (and_15_out, xor_15_out, or_8_out);
  and and_16 (and_16_out, A0, B0);
  or or_6 (or_6_out, and_12_out, and_16_out);
  and and_17 (and_17_out, A1, B1);
  or or_7 (or_7_out, and_13_out, and_17_out);
  or or_8 (or_8_out, and_14_out, and_18_out);
  or or_9 (Cout, and_15_out, and_19_out);
  and and_18 (and_18_out, A2, B2);
  and and_19 (and_19_out, A3, B3);

  // Notes on the sheet:
  //   A
  //   B
endmodule

module full__adder (
  input  A,
  input  B,
  input  Cin,
  output S,
  output Co
);

  wire and_1_out, and_2_out, and_3_out, and_4_out, and_5_out, and_6_out, not_1_out, not_2_out, not_3_out,
       not_4_out, or_1_out;

  not not_1 (not_1_out, B);
  not not_2 (not_2_out, A);
  and and_1 (and_1_out, not_1_out, A);
  and and_2 (and_2_out, B, not_2_out);
  or or_1 (or_1_out, and_1_out, and_2_out);
  and and_3 (and_3_out, A, B);
  not not_3 (not_3_out, Cin);
  not not_4 (not_4_out, or_1_out);
  and and_4 (and_4_out, Cin, or_1_out);
  and and_5 (and_5_out, not_3_out, or_1_out);
  and and_6 (and_6_out, not_4_out, Cin);
  or or_2 (Co, and_4_out, and_3_out);
  or or_3 (S, and_5_out, and_6_out);

  // Notes on the sheet:
  //   A
  //   B
  //   Cin
  //   S
  //   Co
endmodule

module alu (
  input  A0,
  input  A1,
  input  A2,
  input  A3,
  input  A4,
  input  A5,
  input  A6,
  input  A7,
  input  B0,
  input  B1,
  input  B2,
  input  ENABLE,
  input  B3,
  input  B4,
  input  B5,
  input  B6,
  input  B7,
  input  SUBTRACT,
  output S0,
  output S1,
  output S2,
  output S3,
  output S4,
  output S5,
  output S6,
  output S7
);

  wire n4_bit_carry_fast_1_cout, n4_bit_carry_fast_1_s0, n4_bit_carry_fast_1_s1, n4_bit_carry_fast_1_s2,
       n4_bit_carry_fast_1_s3, n4_bit_carry_fast_2_s0, n4_bit_carry_fast_2_s1, n4_bit_carry_fast_2_s2,
       n4_bit_carry_fast_2_s3, xor_1_out, xor_2_out, xor_3_out, xor_4_out, xor_5_out, xor_6_out, xor_7_out,
       xor_8_out;

  xor xor_1 (xor_1_out, SUBTRACT, B0);
  xor xor_2 (xor_2_out, SUBTRACT, B1);
  xor xor_3 (xor_3_out, SUBTRACT, B2);
  xor xor_4 (xor_4_out, SUBTRACT, B3);
  xor xor_5 (xor_5_out, SUBTRACT, B4);
  xor xor_6 (xor_6_out, SUBTRACT, B5);
  xor xor_7 (xor_7_out, SUBTRACT, B6);
  xor xor_8 (xor_8_out, SUBTRACT, B7);
  _4_bit__carry_fast u_4_bit_carry_fast_1 (
    .A0(A0), .A1(A1), .A2(A2), .A3(A3), .B0(xor_1_out), .B1(xor_2_out), .B2(xor_3_out), .B3(xor_4_out),
    .Cin(SUBTRACT), .S0(n4_bit_carry_fast_1_s0), .S1(n4_bit_carry_fast_1_s1), .S2(n4_bit_carry_fast_1_s2),
    .S3(n4_bit_carry_fast_1_s3), .Cout(n4_bit_carry_fast_1_cout));
  _4_bit__carry_fast u_4_bit_carry_fast_2 (
    .A0(A4), .A1(A5), .A2(A6), .A3(A7), .B0(xor_5_out), .B1(xor_6_out), .B2(xor_7_out), .B3(xor_8_out),
    .Cin(n4_bit_carry_fast_1_cout), .S0(n4_bit_carry_fast_2_s0), .S1(n4_bit_carry_fast_2_s1),
    .S2(n4_bit_carry_fast_2_s2), .S3(n4_bit_carry_fast_2_s3));  // open: Cout
  assign S0 = ENABLE ? n4_bit_carry_fast_1_s0 : 1'bz;  // Controlled_Buffer controlled_buffer_1
  assign S1 = ENABLE ? n4_bit_carry_fast_1_s1 : 1'bz;  // Controlled_Buffer controlled_buffer_2
  assign S2 = ENABLE ? n4_bit_carry_fast_1_s2 : 1'bz;  // Controlled_Buffer controlled_buffer_3
  assign S3 = ENABLE ? n4_bit_carry_fast_1_s3 : 1'bz;  // Controlled_Buffer controlled_buffer_4
  assign S4 = ENABLE ? n4_bit_carry_fast_2_s0 : 1'bz;  // Controlled_Buffer controlled_buffer_5
  assign S5 = ENABLE ? n4_bit_carry_fast_2_s1 : 1'bz;  // Controlled_Buffer controlled_buffer_6
  assign S6 = ENABLE ? n4_bit_carry_fast_2_s2 : 1'bz;  // Controlled_Buffer controlled_buffer_7
  assign S7 = ENABLE ? n4_bit_carry_fast_2_s3 : 1'bz;  // Controlled_Buffer controlled_buffer_8
endmodule
